# Fritzing sketch Rx board v1 (saved by Fritzing 0.9.3b)
circuit board: 6.94979cm x 5.91172cm
breadboards: 1

parts:
  Atmega328p1 = atmega328 [package=dip]
  Relay3 = songle relay
  Relay4 = songle relay
  16Mhz1 = Crystal [frequency="16 Mhz" package=THT]
  R2 = Resistor [tolerance=±5% resistance=220 package=THT]
  C3 = Ceramic Capacitor [capacitance=10pF package="100 mil [THT, multilayer]"]
  C4 = Ceramic Capacitor [capacitance=10pF package="100 mil [THT, multilayer]"]
  PWM3 = female pin header, 3 pins [form="♀ (female)"]
  PWM4 = female pin header, 3 pins [form="♀ (female)"]
  Dir3 = female pin header, 3 pins [form="♀ (female)"]
  Dir4 = female pin header, 3 pins [form="♀ (female)"]
  RF_Tx/Rx1 = female pin header, 7 pins [form="♀ (female)"]
  7805 = Voltage Regulator - 5V [package="TO220 [THT]"]
  Input1 = Screw terminal - 2 pins [package=THT]
  Q1 = NPN-Transistor [package="TO92 [THT]"]
  Q2 = NPN-Transistor [package="TO92 [THT]"]
  R3 = Resistor [tolerance=±5% resistance=220 package=THT]
  R4 = Resistor [tolerance=±5% resistance=220 package=THT]
  J1 = female pin header, 2 pins [form="♀ (female)"]
  J2 = RJ45 Jack [package=rj45-8]
  J3 = RJ45 Jack [package=rj45-8]
  Pad10 = Pad [width=2 height=2 connect=center]
  Pad7 = Pad [width=2 height=2 connect=center]
  Pad8 = Pad [width=2 height=2 connect=center]
  Pad9 = Pad [width=2 height=2 connect=center]
  Pad11 = Pad [width=2 height=2 connect=center]
  Pad12 = Pad [width=2 height=2 connect=center]

nets (from the pcb view):
  N1: Atmega328p1.RESET, R2.Pin_1
  N2: Atmega328p1.D0_(RX), RF_Tx/Rx1.pin4
  N3: Atmega328p1.D1_(TX), RF_Tx/Rx1.pin5
  N4: Atmega328p1.D2, J3.3
  N5: Atmega328p1.D3_(PWM), J3.5
  N6: Atmega328p1.D4, J3.7
  N7: Atmega328p1.VCC, Atmega328p1.AVCC, Atmega328p1.AREF, R2.Pin_0, RF_Tx/Rx1.pin2
  N8: Atmega328p1.GND#7, C3.0, C4.1, RF_Tx/Rx1.pin1, Q1.E, Q2.E
  N9: Atmega328p1.XLAT1, 16Mhz1.pin_0, C3.1
  N10: Atmega328p1.XLAT2, 16Mhz1.pin_1, C4.0
  N11: Atmega328p1.D5_(PWM), PWM3.pin2
  N12: Atmega328p1.D6_(PWM), PWM4.pin2
  N13: Atmega328p1.D7, R3.Pin_0
  N14: Atmega328p1.D8, R4.Pin_0
  N15: Atmega328p1.D9_(PWM), J2.6
  N16: Atmega328p1.D10_(PWM), J2.8
  N17: Atmega328p1.D11_(PWM), J2.7
  N18: Atmega328p1.D12, J2.5
  N19: Atmega328p1.D13, J2.3
  N20: Atmega328p1.A0, J3.2
  N21: Atmega328p1.A1, J3.4
  N22: Atmega328p1.A2, J3.6
  N23: Atmega328p1.A3, J3.8
  N24: Atmega328p1.A4, J1.pin2
  N25: Atmega328p1.A5, J1.pin1
  N26: Relay3.VCC, Q2.C
  N27: Relay3.NO, Dir4.pin3
  N28: Relay3.NC, Dir4.pin1
  N29: Relay3.COMMON, Dir4.pin2
  GND: Relay3.GND, Relay4.GND, PWM3.pin3, PWM4.pin3, 7805.output_voltage
  N30: Relay4.VCC, Q1.C
  N31: Relay4.NO, Dir3.pin3
  N32: Relay4.NC, Dir3.pin1
  N33: Relay4.COMMON, Dir3.pin2
  N34: PWM3.pin1, PWM4.pin1
  N35: RF_Tx/Rx1.pin6, Pad10.pad
  N36: RF_Tx/Rx1.pin7, Pad9.pad
  N37: 7805.input_voltage, Input1.pin2
  N38: 7805.GND, Input1.pin1, J2.1, J2.2, J2.4, J3.1
  N39: Q1.B, R3.Pin_1
  N40: Q2.B, R4.Pin_1
  N41: Pad7.pad, Pad8.pad
  N42: Pad11.pad, Pad12.pad

notes:
  ROV Reciever Unit v1.1
