# Fritzing sketch Tx board v1 (saved by Fritzing 0.9.3b)
circuit board: 10.6cm x 5.8cm
breadboards: 2

parts:
  U1 = atmega328 [package=dip]
  R1 = Resistor [tolerance=±5% resistance=220 package=THT]
  16Mhz2 = Crystal [frequency="16 Mhz" package=THT]
  C3 = Ceramic Capacitor [capacitance=10pF package="100 mil [THT, multilayer]"]
  C4 = Ceramic Capacitor [capacitance=10pF package="100 mil [THT, multilayer]"]
  J1 = female pin header, 12 pins [form="♀ (female)"]
  J2 = female pin header, 12 pins [form="♀ (female)"]
  J3 = Generic female header - 7 pins [form="♀ (female)" package=THT]
  J5 = female pin header, 12 pins [form="♀ (female)"]
  J6 = female pin header, 4 pins [form="♀ (female)"]
  J7 = RJ45 Jack [package=rj45-8]
  J8 = RJ45 Jack [package=rj45-8]
  J9 = RJ45 Jack [package=rj45-8]
  Power_plug1 = Power plug
  U2 = Voltage Regulator - 5V [package="TO220 [THT]"]
  Part1 = songle relay
  LED1 = LED - 5mm [color="Red (633nm)" package="5 mm [THT]"]
  LED2 = LED - 5mm [color="Green (565nm)" package="5 mm [THT]"]
  R2 = Resistor [tolerance=±5% resistance=220 package=THT]
  S1 = Toggle Switch [package=THT]
  J10 = Screw terminal - 2 pins [package=THT]
  J11 = female pin header, 4 pins [form="♀ (female)"]
  J12 = female pin header, 2 pins [form="♀ (female)"]
  Pad1 = Pad [width=2 height=1.5 connect=center]
  Pad2 = Pad [width=2 height=1.5 connect=center]
  Pad3 = Pad [width=2 height=1.5 connect=center]
  Pad4 = Pad [width=2 height=1.5 connect=center]
  Pad5 = Pad [width=3 height=2 connect=center]  # not connected
  Pad6 = Pad [width=3 height=2 connect=center]
  Pad7 = Pad [width=3 height=2 connect=center]  # not connected
  Pad8 = Pad [width=3 height=2 connect=center]  # not connected
  Pad11 = Pad [width=3 height=2 connect=center]  # not connected
  Pad9 = Pad [width=3 height=2 connect=center]  # not connected
  Pad12 = Pad [width=3 height=2 connect=center]  # not connected
  Pad10 = Pad [width=3 height=2 connect=center]  # not connected
  Pad13 = Pad [width=3 height=2 connect=center]  # not connected
  Pad15 = Pad [width=3 height=2 connect=center]  # not connected
  Pad16 = Pad [width=3 height=2 connect=center]  # not connected
  Pad14 = Pad [width=3 height=2 connect=center]

nets:
  N1: U1.RESET, R1.Pin_0
  N2: U1.D0_(RX), J3.TXD
  N3: U1.D1_(TX), J3.RXD
  VCC: U1.VCC, U1.AVCC, U1.AREF, R1.Pin_1, J3.VCC, J8.2, U2.output_voltage, Pad6.pad, Pad14.pad
  GND: U1.GND, C3.0, C4.1, J3.GND, J7.1, J8.1, J9.1, Power_plug1.GND, U2.GND, Part1.GND, R2.Pin_1, J10.pin2
  N4: U1.XLAT1, 16Mhz2.pin_0, C3.1
  N5: U1.XLAT2, 16Mhz2.pin_1, C4.0
  N6: U1.D5_(PWM), J7.5
  N7: U1.D6_(PWM), J7.4
  N8: U1.D7, J7.3
  N9: U1.D8, J7.2
  N10: U1.D9_(PWM), J9.5
  N11: U1.D10_(PWM), J9.3
  N12: U1.D11_(PWM), J7.8
  N13: U1.D12, J7.7
  N14: U1.D13, J7.6
  N15: U1.A0, J8.3
  N16: U1.A1, J8.4
  N17: U1.A2, J8.5
  N18: U1.A3, J8.6
  N19: U1.A4, J1.pin3, J8.7, J11.pin3, J12.pin1
  N20: U1.A5, J1.pin4, J8.8, J11.pin4, J12.pin2
  N21: J1.pin1, J11.pin1
  N22: J1.pin2, J11.pin2
  N23: J1.pin5, Pad1.pad
  N24: J1.pin6, Pad2.pad
  N25: J1.pin7, Pad3.pad
  N26: J1.pin8, Pad4.pad
  N27: J1.pin9, J6.pin4
  N28: J1.pin10, J6.pin3
  N29: J1.pin11, J6.pin2
  N30: J1.pin12, J6.pin1
  N31: J2.pin1, J5.pin1
  N32: J2.pin2, J5.pin2
  N33: J2.pin3, J5.pin3
  N34: J2.pin4, J5.pin4
  N35: J2.pin5, J5.pin5
  N36: J2.pin6, J5.pin6
  N37: J2.pin7, J5.pin7
  N38: J2.pin8, J5.pin8
  N39: J2.pin9, J5.pin9
  N40: J2.pin10, J5.pin10
  N41: J2.pin11, J5.pin11
  N42: J2.pin12, J5.pin12
  N43: Power_plug1.VCC, Part1.COMMON, S1.COM, J10.pin1
  N44: U2.input_voltage, Part1.NO, LED2.anode
  N45: Part1.VCC, S1.L1
  N46: Part1.NC, LED1.anode
  N47: LED1.cathode, LED2.cathode, R2.Pin_0

custom parts:
  Generic female header - 7 pins: Generic female header
